# Fritzing sketch Stripboard_49x18 (saved by Fritzing 0.9.6b)
stripboards: 1

parts:
  J3 = male pin header, 2 pins [form="♂ (male)"]
  R1 = Resistor [tolerance=±5% power=0.25 resistance=2.2k package=THT]
  D1 = Rectifier Diode [part_number=1N4001 package="300 mil [THT]"]
  D2 = Rectifier Diode [part_number=1N4001 package="300 mil [THT]"]
  R2 = Resistor [tolerance=±5% power=0.25 resistance=10 package=THT]
  Q1 = PNP-Transistor [package="TO92 [THT]"]
  J4 = male pin header, 4 pins [form="♂ (male)"]
  LED1 = LED - 5mm [color="Red (633nm)" current=0.030 package="5 mm [THT]"]
  R3 = Resistor [tolerance=±5% power=0.25 resistance=330 package=THT]
  J5 = male pin header, 4 pins [form="♂ (male)"]
  J6_GND = male pin header, 4 pins [form="♂ (male)"]
  J7_3V3 = male pin header, 4 pins [form="♂ (male)"]
  C1 = Ceramic Capacitor [capacitance=100nF voltage=35V package="100 mil [THT, multilayer]"]
  R5 = Resistor [tolerance=±5% power=0.25 resistance=10k package=THT]
  U1 = Optocoupler [package=THT]
  J8 = male pin header, 4 pins [form="♂ (male)"]
  J9 = male pin header, 4 pins [form="♂ (male)"]
  C2 = Tantalum Capacitor [capacitance=1μF voltage=35V package="100 mil [THT, tantalum]"]
  D4 = Schottky Diode [part_number=1N5817 package="300 mil [THT]"]
  D5 = Schottky Diode [part_number=1N5817 package="300 mil [THT]"]
  Q2 = NPN-Transistor [package="TO92 [THT]"]
  R6 = Resistor [tolerance=±5% power=0.25 resistance=10k package=THT]
  R7 = Resistor [tolerance=±5% power=0.25 resistance=10k package=THT]
  J10_TEST = male pin header, 2 pins [form="♂ (male)"]
  R8 = Resistor [tolerance=±5% power=0.25 resistance=100k package=THT]

nets:
  N1: J3.pin1, J3.pin2, R1.Pin_0
  N2: R1.Pin_1, D1.anode, D2.cathode, R2.Pin_0
  N3: D1.cathode, D2.anode, Q1.E, J5.pin1, J5.pin2, J5.pin3, J5.pin4, D5.anode
  N4: R2.Pin_1, Q1.B
  N5: Q1.C, R5.Pin_0, D4.anode
  N6: J4.pin1, J4.pin2, J4.pin3, J4.pin4, C1.1, R5.Pin_1, J8.pin1, J8.pin2, J8.pin3, J8.pin4, C2.-, Q2.E, R8.Pin_1
  N7: LED1.cathode, U1.Pin_1
  N8: LED1.anode, R3.Pin_1
  N9: R3.Pin_0, C2.+, D5.cathode
  N10: J6_GND.pin1, J6_GND.pin2, J6_GND.pin3, J6_GND.pin4, U1.Pin_4, J9.pin1, J9.pin2, J9.pin3, J9.pin4
  N11: J7_3V3.pin1, J7_3V3.pin2, J7_3V3.pin3, J7_3V3.pin4, R7.Pin_1
  N12: C1.0, D4.cathode, R6.Pin_0, R8.Pin_0
  N13: U1.Pin_2, Q2.C
  N14: U1.Pin_5, R7.Pin_0, J10_TEST.pin1, J10_TEST.pin2
  N15: Q2.B, R6.Pin_1

notes:
  DCC
  3v3
